// Logisim project CPUMay(Asaad).circ as structural Verilog: 8 circuits, main circuit main
module main (
);

  wire ALUSrc, branchjumpsig_1_jump, branchjumpsig_1_jumpr, bubble, clock_1_out, en, EQ, GT, Kill1, Kill2,
       ld, LT, maincontrolunit_1_alusrc, maincontrolunit_1_rf, multiplexer_4_out, multiplexer_5_out,
       not_1_out, or_1_out, rf, rf1_q, rf2_q, Stall, str;
  wire [1:0] extOp, ForewardA, ForewardB, func, maincontrolunit_1_wb, pcsrc_1_pcsrc, regdest, register_5_q_2,
       register_5_q_3, wb;
  wire [2:0] maincontrolunit_1_ld, Rd0, Rd1_q, Rd2_q, Rd3, register_2_q;
  wire [4:0] mem_q, multiplexer_9_out, OPCODE, register_5_q, undriven;
  wire [5:0] branchjumpsig_1_beqz, register_3_q;
  wire [8:0] alucontrolunitdecoder2_1_aluop, multiplexer_10_out;
  wire [10:2] Instruction_q;
  wire [15:0] multiplexer_2_out, ram_1_data;
  wire [19:0] Branch, extender_1_imm20, Jump, JumpR, multiplexer_1_out, PC, PC_1;
  wire [31:0] alu_1_busd, bit_extender_2_out, DataIn_q, imm11, Imm_q, multiplexer_6_out, multiplexer_7_out,
       multiplexer_8_out, multiplexer_11_out, R0, R1, R2, R3, R4, R5, R6, R7, ram_2_data,
       registerfile_1_sbus, registerfile_1_tbus, rs, rt, wbdata;
  wire [31:20] D_q;

  Register #(.width(20)) register_1 (.D(multiplexer_1_out), .en(not_1_out), .Q(PC), .clk(clock_1_out));  // open: clr
  Clock clock_1 (.out(clock_1_out));
  Multiplexer #(.select(2), .width(20), .disabled(0), .enable("false")) multiplexer_1 (
    .in0(PC_1), .in1(Jump), .in2(Branch), .in3(JumpR), .out(multiplexer_1_out), .sel(pcsrc_1_pcsrc));
  Adder #(.width(20)) adder_1 (.a(PC), .b(20'h1), .out(PC_1));  // open: cin, cout
  Register #(.width(3)) register_2 (.D({LT, EQ, GT}), .Q(register_2_q), .clk(clock_1_out));  // open: en, clr
  // Probe on R2
  // Probe on R5
  // Probe on R7
  PCsrc pcsrc_1 (
    .BEQZ(register_3_q[0]), .BNEZ(register_3_q[1]), .BGEZ(register_3_q[3]), .BGTZ(register_3_q[4]),
    .BLEZ(register_3_q[5]), .BLTZ(register_3_q[2]), .LT(register_2_q[2]), .EQ(register_2_q[1]),
    .GT(register_2_q[0]), .jump(branchjumpsig_1_jump), .PCsrc(pcsrc_1_pcsrc), .JumpR(branchjumpsig_1_jumpr),
    .Kill2(Kill2), .Kill1(Kill1));
  RAM #(.addrWidth(20), .dataWidth(16)) ram_1 (.addr(PC), .data(ram_1_data));  // open: sel, clk, ld, clr
  not not_1 (not_1_out, Stall);
  // Probe on R1
  // Probe on R4
  BranchJumpSig branchjumpsig_1 (
    .BEQZ(branchjumpsig_1_beqz[0]), .BNEZ(branchjumpsig_1_beqz[1]), .BLTZ(branchjumpsig_1_beqz[2]),
    .BGEZ(branchjumpsig_1_beqz[3]), .BGTZ(branchjumpsig_1_beqz[4]), .BLEZ(branchjumpsig_1_beqz[5]),
    .JumpR(branchjumpsig_1_jumpr), .OPcode(OPCODE), .Jump(branchjumpsig_1_jump));
  Register #(.width(16)) Instruction (
    .D(multiplexer_2_out), .en(not_1_out), .Q({OPCODE, Instruction_q, func}), .clk(clock_1_out));  // open: clr
  Multiplexer #(.width(16), .disabled(0), .enable("false")) multiplexer_2 (
    .in0(ram_1_data), .in1({16{1'b0}}), .out(multiplexer_2_out), .sel(Kill1));
  // Probe on R6
  Register #(.width(6)) register_3 (.D(branchjumpsig_1_beqz), .Q(register_3_q), .clk(clock_1_out));  // open: en, clr
  // Probe on R0
  // Probe on R3
  Register #(.width(3)) Rd2 (.D(Rd1_q), .Q(Rd2_q), .clk(clock_1_out));  // open: en, clr
  Register #(.width(3)) Rd1 (.D(Rd0), .Q(Rd1_q), .clk(clock_1_out));  // open: en, clr
  Adder #(.width(20)) adder_2 (.a(PC), .b(extender_1_imm20), .out(Jump));  // open: cin, cout
  extender extender_1 (.in_1({Instruction_q, func}), .extOp(extOp), .imm20(extender_1_imm20));
  Multiplexer #(.select(2), .width(3), .disabled(0), .enable("false")) multiplexer_3 (
    .in0(Instruction_q[4:2]), .in1(Instruction_q[7:5]), .in2(3'b111), .in3(3'b000), .out(Rd0), .sel(regdest));
  Register #(.width(3)) u_Rd3 (.D(Rd2_q), .Q(Rd3), .clk(clock_1_out));  // open: en, clr
  Register #(.width(20)) register_4 (.D(Jump), .Q(Branch), .clk(clock_1_out));  // open: en, clr
  assign imm11 = {{12{extender_1_imm20[19]}}, extender_1_imm20};  // Bit_Extender bit_extender_1
  Multiplexer #(.disabled(0), .enable("false")) multiplexer_4 (
    .in0(maincontrolunit_1_alusrc), .in1(1'b0), .out(multiplexer_4_out), .sel(bubble));
  MainControlUnit maincontrolunit_1 (
    .ALUSrc(maincontrolunit_1_alusrc), .ld(maincontrolunit_1_ld[0]), .str(maincontrolunit_1_ld[1]),
    .OPcode(OPCODE), .wb(maincontrolunit_1_wb), .regDest(regdest), .en(maincontrolunit_1_ld[2]),
    .extOp(extOp), .rf(maincontrolunit_1_rf));
  Multiplexer #(.disabled(0), .enable("false")) multiplexer_5 (
    .in0(maincontrolunit_1_rf), .in1(1'b0), .out(multiplexer_5_out), .sel(or_1_out));
  Register #(.width(1)) rf1 (.D(multiplexer_5_out), .Q(rf1_q), .clk(clock_1_out));  // open: en, clr
  ForwardStall2 forwardstall2_1 (
    .Rd1(Rd1_q), .Rd2(Rd2_q), .Rd3(Rd3), .Rt(Instruction_q[7:5]), .Rs(Instruction_q[10:8]), .ld(mem_q[0]),
    .rf1(rf1_q), .rf2(rf2_q), .rf3(rf), .FA(ForewardA), .stall(Stall), .FB(ForewardB));
  Register #(.width(32)) Imm (.D(imm11), .Q(Imm_q), .clk(clock_1_out));  // open: en, clr
  RegisterFile registerfile_1 (
    .Rd(Rd3), .writeSig(rf), .dBus(wbdata), .CLK(clock_1_out), .R0(R0), .sBus(registerfile_1_sbus),
    .tBus(registerfile_1_tbus), .Rs(Instruction_q[10:8]), .Rt(Instruction_q[7:5]), .R1(R1), .R2(R2), .R3(R3),
    .R4(R4), .R5(R5), .R6(R6), .R7(R7));
  Register #(.width(1)) u_ALUSrc (.D(multiplexer_4_out), .Q(ALUSrc), .clk(clock_1_out));  // open: en, clr
  Register #(.width(1)) rf3 (.D(rf2_q), .Q(rf), .clk(clock_1_out));  // open: en, clr
  Register #(.width(1)) rf2 (.D(rf1_q), .Q(rf2_q), .clk(clock_1_out));  // open: en, clr
  Multiplexer #(.width(32), .disabled(0), .enable("false")) multiplexer_6 (
    .in0(rt), .in1(Imm_q), .out(multiplexer_6_out), .sel(ALUSrc));
  or or_1 (or_1_out, Stall, Kill2);
  Multiplexer #(.select(2), .width(32), .disabled(0), .enable("false")) multiplexer_7 (
    .in0(registerfile_1_sbus), .in1(alu_1_busd), .in2(multiplexer_11_out), .in3(wbdata),
    .out(multiplexer_7_out), .sel(ForewardA));
  Register #(.width(32)) A (.D(multiplexer_7_out), .Q(rs), .clk(clock_1_out));  // open: en, clr
  Multiplexer #(.select(2), .width(32), .disabled(0), .enable("false")) multiplexer_8 (
    .in0(registerfile_1_tbus), .in1(alu_1_busd), .in2(multiplexer_11_out), .in3(wbdata),
    .out(multiplexer_8_out), .sel(ForewardB));
  Register #(.width(32)) B (.D(multiplexer_8_out), .Q(rt), .clk(clock_1_out));  // open: en, clr
  Register #(.width(5)) mem (.D(multiplexer_9_out), .Q(mem_q), .clk(clock_1_out));  // open: en, clr
  Multiplexer #(.width(5), .disabled(0), .enable("false")) multiplexer_9 (
    .in0({maincontrolunit_1_wb, maincontrolunit_1_ld}), .in1(undriven), .out(multiplexer_9_out),
    .sel(or_1_out));
  ALU_ALU alu_1 (
    .LogicOp(register_5_q_3), .ShitfOp(register_5_q_2), .Sub(register_5_q[4]), .Branch(register_5_q[3]),
    .Unsigned(register_5_q[2]), .ALUOp(register_5_q[1:0]), .BusB(multiplexer_6_out), .BusA(rs),
    .BusD(alu_1_busd), .out_9(GT), .out_10(EQ), .out_11(LT));
  Multiplexer #(.width(9), .disabled(0), .enable("false")) multiplexer_10 (
    .in0(alucontrolunitdecoder2_1_aluop), .in1({9{1'b0}}), .out(multiplexer_10_out), .sel(bubble));
  ALUControlUnitDecoder2 alucontrolunitdecoder2_1 (
    .OPcode(OPCODE), .\function (func), .LogicOp(alucontrolunitdecoder2_1_aluop[8:7]),
    .Unsigned(alucontrolunitdecoder2_1_aluop[2]), .Sub(alucontrolunitdecoder2_1_aluop[4]),
    .ShiftOp(alucontrolunitdecoder2_1_aluop[6:5]), .ALUOp(alucontrolunitdecoder2_1_aluop[1:0]),
    .Branch(alucontrolunitdecoder2_1_aluop[3]));
  Register #(.width(5)) mem_2 (.D(mem_q), .Q({wb, en, str, ld}), .clk(clock_1_out));  // open: en, clr
  Register #(.width(9)) register_5 (
    .D(multiplexer_10_out), .Q({register_5_q_3, register_5_q_2, register_5_q}), .clk(clock_1_out));  // open: en, clr
  or or_2 (bubble, Stall, Kill2);
  Register #(.width(32)) D (.D(alu_1_busd), .Q({D_q, JumpR}), .clk(clock_1_out));  // open: en, clr
  Multiplexer #(.select(2), .width(32), .disabled(0), .enable("false")) multiplexer_11 (
    .in0({D_q, JumpR}), .in1(ram_2_data), .in2(bit_extender_2_out), .in3(imm11), .out(multiplexer_11_out),
    .sel(wb));
  Register #(.width(32)) DataOut (.D(multiplexer_11_out), .Q(wbdata), .clk(clock_1_out));  // open: en, clr
  assign bit_extender_2_out = {{12{1'b0}}, PC_1};  // Bit_Extender bit_extender_2
  Register #(.width(32)) DataIn (.D(rt), .Q(DataIn_q), .clk(clock_1_out));  // open: en, clr
  RAM #(.addrWidth(20), .dataWidth(32), .bus("separate")) ram_2 (
    .addr(JumpR), .din(DataIn_q), .data(ram_2_data), .str(str), .sel(en), .clk(clock_1_out), .ld(ld));  // open: clr
endmodule

// RF
module RegisterFile (
  input  [2:0] Rd,
  input  writeSig,
  input  [2:0] Rs,
  input  [31:0] dBus,
  input  CLK,
  input  [2:0] Rt,
  output [31:0] sBus,
  output [31:0] tBus,
  output [31:0] R0,
  output [31:0] R1,
  output [31:0] R2,
  output [31:0] R3,
  output [31:0] R4,
  output [31:0] R5,
  output [31:0] R6,
  output [31:0] R7
);

  wire and_1_out, and_2_out, and_3_out, and_4_out, and_5_out, and_6_out, and_7_out, and_8_out, buf0, buf1,
       buf2, buf3, buf4, buf5, buf6, buf7, buf8, buf9, buf10, buf11, buf12, buf13, buf14, buf15,
       decoder_1_out0, decoder_1_out1, decoder_1_out2, decoder_1_out3, decoder_1_out4, decoder_1_out5,
       decoder_1_out6, decoder_1_out7;

  and and_1 (and_1_out, decoder_1_out0, writeSig);
  Decoder #(.select(3), .enable("false")) decoder_1 (
    .out0(decoder_1_out0), .out1(decoder_1_out1), .out2(decoder_1_out2), .out3(decoder_1_out3),
    .out4(decoder_1_out4), .out5(decoder_1_out5), .out6(decoder_1_out6), .out7(decoder_1_out7), .sel(Rd));
  Register #(.width(32)) u_r0 (.D(dBus), .en(and_1_out), .Q(R0), .clk(CLK));  // open: clr
  and and_2 (and_2_out, decoder_1_out1, writeSig);
  Register #(.width(32)) u_r1 (.D(dBus), .en(and_2_out), .Q(R1), .clk(CLK));  // open: clr
  assign sBus = buf0 ? R0 : 32'bz;  // Controlled_Buffer controlled_buffer_1
  assign tBus = buf8 ? R0 : 32'bz;  // Controlled_Buffer controlled_buffer_2
  and and_3 (and_3_out, decoder_1_out2, writeSig);
  Register #(.width(32)) u_r2 (.D(dBus), .en(and_3_out), .Q(R2), .clk(CLK));  // open: clr
  assign sBus = buf1 ? R1 : 32'bz;  // Controlled_Buffer controlled_buffer_3
  assign tBus = buf9 ? R1 : 32'bz;  // Controlled_Buffer controlled_buffer_4
  and and_4 (and_4_out, decoder_1_out3, writeSig);
  assign tBus = buf10 ? R2 : 32'bz;  // Controlled_Buffer controlled_buffer_5
  and and_5 (and_5_out, decoder_1_out4, writeSig);
  Register #(.width(32)) u_r3 (.D(dBus), .en(and_4_out), .Q(R3), .clk(CLK));  // open: clr
  assign sBus = buf2 ? R2 : 32'bz;  // Controlled_Buffer controlled_buffer_6
  and and_6 (and_6_out, decoder_1_out5, writeSig);
  Register #(.width(32)) u_r4 (.D(dBus), .en(and_5_out), .Q(R4), .clk(CLK));  // open: clr
  assign sBus = buf3 ? R3 : 32'bz;  // Controlled_Buffer controlled_buffer_7
  assign tBus = buf11 ? R3 : 32'bz;  // Controlled_Buffer controlled_buffer_8
  Register #(.width(32)) u_r5 (.D(dBus), .en(and_6_out), .Q(R5), .clk(CLK));  // open: clr
  assign sBus = buf4 ? R4 : 32'bz;  // Controlled_Buffer controlled_buffer_9
  assign tBus = buf12 ? R4 : 32'bz;  // Controlled_Buffer controlled_buffer_10
  and and_7 (and_7_out, decoder_1_out6, writeSig);
  Register #(.width(32)) u_r6 (.D(dBus), .en(and_7_out), .Q(R6), .clk(CLK));  // open: clr
  assign sBus = buf5 ? R5 : 32'bz;  // Controlled_Buffer controlled_buffer_11
  assign tBus = buf13 ? R5 : 32'bz;  // Controlled_Buffer controlled_buffer_12
  and and_8 (and_8_out, decoder_1_out7, writeSig);
  assign sBus = buf6 ? R6 : 32'bz;  // Controlled_Buffer controlled_buffer_13
  assign tBus = buf14 ? R6 : 32'bz;  // Controlled_Buffer controlled_buffer_14
  Register #(.width(32)) u_r7 (.D(dBus), .en(and_8_out), .Q(R7), .clk(CLK));  // open: clr
  Decoder #(.select(3), .enable("false")) decoder_2 (
    .out0(buf0), .out1(buf1), .out2(buf2), .out3(buf3), .out4(buf4), .out5(buf5), .out6(buf6), .out7(buf7),
    .sel(Rs));
  Decoder #(.select(3), .enable("false")) decoder_3 (
    .out0(buf8), .out1(buf9), .out2(buf10), .out3(buf11), .out4(buf12), .out5(buf13), .out6(buf14),
    .out7(buf15), .sel(Rt));
  assign sBus = buf7 ? R7 : 32'bz;  // Controlled_Buffer controlled_buffer_15
  assign tBus = buf15 ? R7 : 32'bz;  // Controlled_Buffer controlled_buffer_16
endmodule

// logic
module Logic_Unit (
  input  [31:0] Rs,
  input  [31:0] Rt,
  input  [1:0] contSig,
  output [31:0] Rd
);

  wire [31:0] and_1_out, and_2_out, not_1_out, or_1_out, xor_1_out;

  assign not_1_out = ~Rs;  // NOT_Gate not_1, 32 bits wide
  assign and_1_out = Rs & Rt;  // AND_Gate and_1, 32 bits wide
  assign and_2_out = not_1_out & Rt;  // AND_Gate and_2, 32 bits wide
  assign or_1_out = Rs | Rt;  // OR_Gate or_1, 32 bits wide
  assign xor_1_out = Rs ^ Rt;  // XOR_Gate xor_1, 32 bits wide
  Multiplexer #(.select(2), .width(32), .enable("false")) multiplexer_1 (
    .in0(and_1_out), .in1(and_2_out), .in2(or_1_out), .in3(xor_1_out), .out(Rd), .sel(contSig));
endmodule

// shifter
module Shifter (
  input  [31:0] Rs,
  input  [4:0] Imm,
  input  [1:0] contSig,
  output [31:0] Rt
);

  wire [31:0] shifter_1_out, shifter_2_out, shifter_3_out, shifter_4_out;

  Shifter_part #(.width(32)) shifter_1 (.in(Rs), .\dist (Imm), .out(shifter_1_out));
  Shifter_part #(.width(32), .shift("lr")) shifter_2 (.in(Rs), .\dist (Imm), .out(shifter_2_out));
  Shifter_part #(.width(32), .shift("ar")) shifter_3 (.in(Rs), .\dist (Imm), .out(shifter_3_out));
  Shifter_part #(.width(32), .shift("rr")) shifter_4 (.in(Rs), .\dist (Imm), .out(shifter_4_out));
  Multiplexer #(.select(2), .width(32), .enable("false")) multiplexer_1 (
    .in0(shifter_1_out), .in1(shifter_2_out), .in2(shifter_3_out), .in3(shifter_4_out), .out(Rt),
    .sel(contSig));
endmodule

module ALU (
  input  [1:0] LogicContSig,
  input  [31:0] Rs,
  input  [31:0] Rt,
  input  [1:0] ALUContSig,
  input  [1:0] ShiftContSig,
  input  invSig,
  input  zeroComp,
  output [31:0] Rd,
  output [1:0] flags
);

  wire comparator_1_eq, comparator_1_gt, comparator_2_eq, comparator_2_gt;
  wire [31:0] adder_1_out, bit_extender_1_out, logic_unit_1_rd, multiplexer_1_out, shifter_1_rt, xor_1_out;

  assign bit_extender_1_out = {{31{invSig}}, invSig};  // Bit_Extender bit_extender_1
  assign xor_1_out = Rs ^ bit_extender_1_out;  // XOR_Gate xor_1, 32 bits wide
  Multiplexer #(.width(32), .enable("false")) multiplexer_1 (
    .in0(Rt), .in1({32{1'b0}}), .out(multiplexer_1_out), .sel(zeroComp));
  Shifter shifter_1 (.Rs(Rs), .Imm(Rt[4:0]), .contSig(ShiftContSig), .Rt(shifter_1_rt));
  Logic_Unit logic_unit_1 (.Rs(Rs), .Rt(Rt), .contSig(LogicContSig), .Rd(logic_unit_1_rd));
  Adder #(.width(32)) adder_1 (.a(xor_1_out), .b(Rt), .out(adder_1_out), .cin(invSig));  // open: cout
  Comparator #(.width(32)) comparator_1 (
    .a(Rs), .b(multiplexer_1_out), .gt(comparator_1_gt), .eq(comparator_1_eq));  // open: lt
  Comparator #(.width(32), .mode("unsigned")) comparator_2 (
    .a(Rs), .b(multiplexer_1_out), .gt(comparator_2_gt), .eq(comparator_2_eq));  // open: lt
  Multiplexer #(.enable("false")) multiplexer_2 (
    .in0(comparator_1_gt), .in1(comparator_2_gt), .out(flags[0]), .sel(invSig));
  Multiplexer #(.enable("false")) multiplexer_3 (
    .in0(comparator_1_eq), .in1(comparator_2_eq), .out(flags[1]), .sel(zeroComp));
  Multiplexer #(.select(2), .width(32), .enable("false")) multiplexer_4 (
    .in0(logic_unit_1_rd), .in1(adder_1_out), .in3(shifter_1_rt), .out(Rd), .sel(ALUContSig));  // open: in2
endmodule

module extender (
  input  [10:0] in_1,
  input  [1:0] extOp,
  output [19:0] imm20
);

  wire [19:0] bit_extender_1_out, bit_extender_2_out, bit_extender_3_out;

  assign bit_extender_1_out = {{15{in_1[4]}}, in_1[4:0]};  // Bit_Extender bit_extender_1
  assign bit_extender_2_out = {{12{in_1[7]}}, in_1[7:0]};  // Bit_Extender bit_extender_2
  assign bit_extender_3_out = {{9{in_1[10]}}, in_1};  // Bit_Extender bit_extender_3
  Multiplexer #(.select(2), .width(20), .disabled(0), .enable("false")) multiplexer_1 (
    .in0(bit_extender_1_out), .in1(bit_extender_2_out), .in2(bit_extender_3_out), .out(imm20), .sel(extOp));  // open: in3

  // Notes on the sheet:
  //   5imm
  //   8imm
  //   11imm
endmodule

// ALUV2
module ALU_Asaad (
  input  [31:0] Rs,
  input  [31:0] Rt,
  input  [6:0] ALUOp,
  output [31:0] Rd,
  output Negative,
  output Zero
);

  wire adder_1_cout, invSig, xor_2_out, zeroComp;
  wire [1:0] ALUCont, logicCont, ShiftContSig;
  wire [3:2] rom_1_data;
  wire [15:0] not_2_out, or_1_out;
  wire [31:0] adder_1_out, bit_extender_1_out, bit_extender_2_out, logic_unit_1_rd, shifter_1_rt, xor_1_out;

  assign bit_extender_1_out = {{31{invSig}}, invSig};  // Bit_Extender bit_extender_1
  ROM #(.addrWidth(7), .dataWidth(10)) rom_1 (
    .addr(ALUOp), .data({zeroComp, invSig, logicCont, ALUCont, rom_1_data, ShiftContSig}));  // open: sel
  assign xor_1_out = Rs ^ bit_extender_1_out;  // XOR_Gate xor_1, 32 bits wide
  Shifter shifter_1 (.Rs(Rs), .Imm(Rt[4:0]), .contSig(ShiftContSig), .Rt(shifter_1_rt));
  Logic_Unit logic_unit_1 (.Rs(Rs), .Rt(Rt), .contSig(logicCont), .Rd(logic_unit_1_rd));
  Adder #(.width(32)) adder_1 (.a(xor_1_out), .b(Rt), .out(adder_1_out), .cin(invSig), .cout(adder_1_cout));
  not not_1 (Negative, adder_1_cout);
  xor xor_2 (xor_2_out, adder_1_out[31], adder_1_cout);
  assign bit_extender_2_out = {{31{1'b0}}, xor_2_out};  // Bit_Extender bit_extender_2
  Multiplexer #(.select(2), .width(32), .enable("false")) multiplexer_1 (
    .in0(logic_unit_1_rd), .in1(adder_1_out), .in2(bit_extender_2_out), .in3(shifter_1_rt), .out(Rd),
    .sel(ALUCont));
  assign or_1_out = Rd[31:16] | Rd[15:0];  // OR_Gate or_1, 16 bits wide
  assign not_2_out = ~or_1_out;  // NOT_Gate not_2, 16 bits wide
  Bit_Extender #(.in_width(16), .out_width(1), .\type ("sign")) bit_extender_3 (.in(not_2_out), .out(Zero));

  // Notes on the sheet:
  //   Should ROM be here? to be discussed
endmodule

// PCSrc
module PCsrc (
  input  JumpR,
  input  jump,
  input  LT,
  input  EQ,
  input  GT,
  input  BEQZ,
  input  BNEZ,
  input  BGEZ,
  input  BGTZ,
  input  BLEZ,
  input  BLTZ,
  output [1:0] PCsrc,
  output Kill2,
  output Kill1
);

  wire and_1_out, and_2_out, and_3_out, and_4_out, and_5_out, and_6_out, or_4_out, or_5_out;

  or or_1 (Kill1, PCsrc[0], Kill2);
  or or_2 (PCsrc[0], JumpR, jump);
  or or_3 (Kill2, and_1_out, and_2_out, and_3_out, JumpR, and_4_out, and_5_out, and_6_out);
  and and_1 (and_1_out, EQ, BEQZ);
  and and_2 (and_2_out, BNEZ, ~EQ);  // AND_Gate
  and and_3 (and_3_out, BGEZ, or_4_out);
  and and_4 (and_4_out, GT, BGTZ);
  and and_5 (and_5_out, BLEZ, or_5_out);
  and and_6 (and_6_out, BLTZ, LT);
  or or_4 (or_4_out, EQ, GT);
  or or_5 (or_5_out, LT, EQ);

  assign PCsrc[1] = Kill2;
endmodule
