// Logisim project CPUPipeLined.circ as structural Verilog: 5 circuits, main circuit main
module main (
);

  wire clock_1_out, en, ld, PC2, rf, rsmux, str, wb;
  wire [1:0] ALUCont, logcont, PC4, regdest, Shift;
  wire [2:0] multiplexer_3_out, mux9;
  wire [6:5] rom_1_data;
  wire [15:0] ram_1_data;
  wire [19:0] adder_1_out, bit_extender_1_out, bit_extender_2_out, multiplexer_1_out, multiplexer_2_out,
       register_1_q;
  wire [31:0] alu_1_p7, bit_extender_3_out, bit_extender_4_out, multiplexer_4_out, multiplexer_5_out, R0, R1,
       R2, R3, R4, R5, R6, R7, ram_2_data, registerfile_1_sbus, registerfile_1_tbus, wbdata;
  wire [31:20] bit_extender_1_out_2, bit_extender_2_out_2;

  Multiplexer #(.width(20), .enable("false")) multiplexer_1 (
    .in0(register_1_q), .in1(multiplexer_5_out[19:0]), .out(multiplexer_1_out), .sel(PC2));
  Clock clock_1 (.out(clock_1_out));
  Multiplexer #(.select(2), .width(20), .enable("false")) multiplexer_2 (
    .in0(20'h1), .in1(bit_extender_1_out), .in2(bit_extender_2_out), .in3(alu_1_p7[19:0]),
    .out(multiplexer_2_out), .sel(PC4));
  Register #(.width(20)) register_1 (.D(adder_1_out), .en(1'b1), .Q(register_1_q), .clk(clock_1_out));  // open: clr
  // Probe on R2
  // Probe on R5
  // Probe on R7
  Adder #(.width(20)) adder_1 (.a(multiplexer_2_out), .b(multiplexer_1_out), .out(adder_1_out));  // open: cin, cout
  // Probe on R1
  // Probe on R4
  RAM #(.addrWidth(20), .dataWidth(16)) ram_1 (.addr(register_1_q), .data(ram_1_data));  // open: sel, clk, ld, clr
  // Probe on R6
  // Probe on R0
  // Probe on R3
  assign {bit_extender_1_out_2, bit_extender_1_out} = {{21{ram_1_data[10]}}, ram_1_data[10:0]};  // Bit_Extender bit_extender_1
  assign {bit_extender_2_out_2, bit_extender_2_out} = {{24{ram_1_data[7]}}, ram_1_data[7:0]};  // Bit_Extender bit_extender_2
  assign bit_extender_3_out = {{27{ram_1_data[4]}}, ram_1_data[4:0]};  // Bit_Extender bit_extender_3
  assign bit_extender_4_out = {{12{1'b0}}, register_1_q};  // Bit_Extender bit_extender_4
  Multiplexer #(.select(2), .width(3), .enable("false")) multiplexer_3 (
    .in0(ram_1_data[4:2]), .in1(ram_1_data[7:5]), .in2(3'b111), .out(multiplexer_3_out), .sel(regdest));  // open: in3
  ROM #(.addrWidth(5), .dataWidth(22)) rom_1 (
    .addr(ram_1_data[15:11]),
    .data({PC2, PC4, regdest, mux9, wb, rf, str, ld, en, logcont, rom_1_data, Shift, ALUCont, rsmux}),
    .sel(1'b1));
  RegisterFile registerfile_1 (
    .Rd(multiplexer_3_out), .writeSig(rf), .dBus(wbdata), .CLK(clock_1_out), .R0(R0),
    .sBus(registerfile_1_sbus), .tBus(registerfile_1_tbus), .Rs(ram_1_data[10:8]), .Rt(ram_1_data[7:5]),
    .R1(R1), .R2(R2), .R3(R3), .R4(R4), .R5(R5), .R6(R6), .R7(R7));
  Multiplexer #(.select(3), .width(32), .enable("false")) multiplexer_4 (
    .in0({bit_extender_1_out_2, bit_extender_1_out}), .in1({bit_extender_2_out_2, bit_extender_2_out}),
    .in2(bit_extender_3_out), .in3(bit_extender_4_out), .in4(registerfile_1_tbus), .out(multiplexer_4_out),
    .sel(mux9));  // open: in5, in6, in7
  Multiplexer #(.width(32), .enable("false")) multiplexer_5 (
    .in0(registerfile_1_sbus), .in1(32'h1), .out(multiplexer_5_out), .sel(rsmux));
  Multiplexer #(.width(32), .enable("false")) multiplexer_6 (.in0(alu_1_p7), .in1(ram_2_data), .out(wbdata), .sel(wb));
  // ALU alu_1: pin names not known; wires that end beside it: logcont, multiplexer_5_out, multiplexer_4_out, ALUCont, ram_1_data[1:0], Shift, alu_1_p7
  RAM #(.addrWidth(20), .dataWidth(32), .bus("separate")) ram_2 (
    .addr(alu_1_p7[19:0]), .din(registerfile_1_tbus), .data(ram_2_data), .str(str), .sel(en),
    .clk(clock_1_out), .ld(ld));  // open: clr

  // Notes on the sheet:
  //   Should PC be here?
  //   contents of rom_1 (hex, n*v repeats v):
  //   11000 11002 0 0 29000 29080 29100 29182 29002 29042 29002 29002 29006 2900e 29016 2901e 2b602 28a02
  //   0 0 6*124022 12c002 341003 21002 21002 a0002 2cd003
endmodule

// RF
module RegisterFile (
  input  [2:0] Rd,
  input  writeSig,
  input  [2:0] Rs,
  input  [31:0] dBus,
  input  CLK,
  input  [2:0] Rt,
  output [31:0] sBus,
  output [31:0] tBus,
  output [31:0] R0,
  output [31:0] R1,
  output [31:0] R2,
  output [31:0] R3,
  output [31:0] R4,
  output [31:0] R5,
  output [31:0] R6,
  output [31:0] R7
);

  wire and_1_out, and_2_out, and_3_out, and_4_out, and_5_out, and_6_out, and_7_out, and_8_out, buf0, buf1,
       buf2, buf3, buf4, buf5, buf6, buf7, buf8, buf9, buf10, buf11, buf12, buf13, buf14, buf15,
       decoder_1_out0, decoder_1_out1, decoder_1_out2, decoder_1_out3, decoder_1_out4, decoder_1_out5,
       decoder_1_out6, decoder_1_out7;

  and and_1 (and_1_out, decoder_1_out0, writeSig);
  Decoder #(.select(3), .enable("false")) decoder_1 (
    .out0(decoder_1_out0), .out1(decoder_1_out1), .out2(decoder_1_out2), .out3(decoder_1_out3),
    .out4(decoder_1_out4), .out5(decoder_1_out5), .out6(decoder_1_out6), .out7(decoder_1_out7), .sel(Rd));
  Register #(.width(32)) u_r0 (.D(dBus), .en(and_1_out), .Q(R0), .clk(CLK));  // open: clr
  and and_2 (and_2_out, decoder_1_out1, writeSig);
  Register #(.width(32)) u_r1 (.D(dBus), .en(and_2_out), .Q(R1), .clk(CLK));  // open: clr
  assign sBus = buf0 ? R0 : 32'bz;  // Controlled_Buffer controlled_buffer_1
  assign tBus = buf8 ? R0 : 32'bz;  // Controlled_Buffer controlled_buffer_2
  and and_3 (and_3_out, decoder_1_out2, writeSig);
  Register #(.width(32)) u_r2 (.D(dBus), .en(and_3_out), .Q(R2), .clk(CLK));  // open: clr
  assign sBus = buf1 ? R1 : 32'bz;  // Controlled_Buffer controlled_buffer_3
  assign tBus = buf9 ? R1 : 32'bz;  // Controlled_Buffer controlled_buffer_4
  and and_4 (and_4_out, decoder_1_out3, writeSig);
  assign tBus = buf10 ? R2 : 32'bz;  // Controlled_Buffer controlled_buffer_5
  and and_5 (and_5_out, decoder_1_out4, writeSig);
  Register #(.width(32)) u_r3 (.D(dBus), .en(and_4_out), .Q(R3), .clk(CLK));  // open: clr
  assign sBus = buf2 ? R2 : 32'bz;  // Controlled_Buffer controlled_buffer_6
  and and_6 (and_6_out, decoder_1_out5, writeSig);
  Register #(.width(32)) u_r4 (.D(dBus), .en(and_5_out), .Q(R4), .clk(CLK));  // open: clr
  assign sBus = buf3 ? R3 : 32'bz;  // Controlled_Buffer controlled_buffer_7
  assign tBus = buf11 ? R3 : 32'bz;  // Controlled_Buffer controlled_buffer_8
  Register #(.width(32)) u_r5 (.D(dBus), .en(and_6_out), .Q(R5), .clk(CLK));  // open: clr
  assign sBus = buf4 ? R4 : 32'bz;  // Controlled_Buffer controlled_buffer_9
  assign tBus = buf12 ? R4 : 32'bz;  // Controlled_Buffer controlled_buffer_10
  and and_7 (and_7_out, decoder_1_out6, writeSig);
  Register #(.width(32)) u_r6 (.D(dBus), .en(and_7_out), .Q(R6), .clk(CLK));  // open: clr
  assign sBus = buf5 ? R5 : 32'bz;  // Controlled_Buffer controlled_buffer_11
  assign tBus = buf13 ? R5 : 32'bz;  // Controlled_Buffer controlled_buffer_12
  and and_8 (and_8_out, decoder_1_out7, writeSig);
  assign sBus = buf6 ? R6 : 32'bz;  // Controlled_Buffer controlled_buffer_13
  assign tBus = buf14 ? R6 : 32'bz;  // Controlled_Buffer controlled_buffer_14
  Register #(.width(32)) u_r7 (.D(dBus), .en(and_8_out), .Q(R7), .clk(CLK));  // open: clr
  Decoder #(.select(3), .enable("false")) decoder_2 (
    .out0(buf0), .out1(buf1), .out2(buf2), .out3(buf3), .out4(buf4), .out5(buf5), .out6(buf6), .out7(buf7),
    .sel(Rs));
  Decoder #(.select(3), .enable("false")) decoder_3 (
    .out0(buf8), .out1(buf9), .out2(buf10), .out3(buf11), .out4(buf12), .out5(buf13), .out6(buf14),
    .out7(buf15), .sel(Rt));
  assign sBus = buf7 ? R7 : 32'bz;  // Controlled_Buffer controlled_buffer_15
  assign tBus = buf15 ? R7 : 32'bz;  // Controlled_Buffer controlled_buffer_16
endmodule

// logic
module Logic_Unit (
  input  [31:0] Rs,
  input  [31:0] Rt,
  input  [1:0] contSig,
  output [31:0] Rd
);

  wire [31:0] and_1_out, and_2_out, not_1_out, or_1_out, xor_1_out;

  assign not_1_out = ~Rs;  // NOT_Gate not_1, 32 bits wide
  assign and_1_out = Rs & Rt;  // AND_Gate and_1, 32 bits wide
  assign and_2_out = not_1_out & Rt;  // AND_Gate and_2, 32 bits wide
  assign or_1_out = Rs | Rt;  // OR_Gate or_1, 32 bits wide
  assign xor_1_out = Rs ^ Rt;  // XOR_Gate xor_1, 32 bits wide
  Multiplexer #(.select(2), .width(32), .enable("false")) multiplexer_1 (
    .in0(and_1_out), .in1(and_2_out), .in2(or_1_out), .in3(xor_1_out), .out(Rd), .sel(contSig));
endmodule

// shifter
module Shifter (
  input  [31:0] Rs,
  input  [4:0] Imm,
  input  [1:0] contSig,
  output [31:0] Rt
);

  wire [31:0] shifter_1_out, shifter_2_out, shifter_3_out, shifter_4_out;

  Shifter_part #(.width(32)) shifter_1 (.in(Rs), .\dist (Imm), .out(shifter_1_out));
  Shifter_part #(.width(32), .shift("lr")) shifter_2 (.in(Rs), .\dist (Imm), .out(shifter_2_out));
  Shifter_part #(.width(32), .shift("ar")) shifter_3 (.in(Rs), .\dist (Imm), .out(shifter_3_out));
  Shifter_part #(.width(32), .shift("rr")) shifter_4 (.in(Rs), .\dist (Imm), .out(shifter_4_out));
  Multiplexer #(.select(2), .width(32), .enable("false")) multiplexer_1 (
    .in0(shifter_1_out), .in1(shifter_2_out), .in2(shifter_3_out), .in3(shifter_4_out), .out(Rt),
    .sel(contSig));
endmodule

module ALU (
  input  [1:0] LogicContSig,
  input  [31:0] Rs,
  input  [31:0] Rt,
  input  [1:0] ALUContSig,
  input  [1:0] ShiftContSig,
  input  [1:0] \function ,
  output [31:0] Rd,
  output [1:0] flags
);

  wire comparator_1_eq, comparator_1_gt, comparator_2_eq, comparator_2_gt, decoder_1_out0, decoder_1_out1;
  wire [31:0] adder_1_out, bit_extender_1_out, logic_unit_1_rd, multiplexer_1_out, shifter_1_rt, xor_1_out;

  Decoder #(.select(2), .disabled(0)) decoder_1 (
    .out0(decoder_1_out0), .out1(decoder_1_out1), .sel(\function ), .en(1'b1));  // open: out2, out3
  assign bit_extender_1_out = {{31{decoder_1_out0}}, decoder_1_out0};  // Bit_Extender bit_extender_1
  assign xor_1_out = Rs ^ bit_extender_1_out;  // XOR_Gate xor_1, 32 bits wide
  Multiplexer #(.width(32), .enable("false")) multiplexer_1 (
    .in0(Rt), .in1({32{1'b0}}), .out(multiplexer_1_out), .sel(decoder_1_out1));
  Shifter shifter_1 (.Rs(Rs), .Imm(Rt[4:0]), .contSig(ShiftContSig), .Rt(shifter_1_rt));
  Logic_Unit logic_unit_1 (.Rs(Rs), .Rt(Rt), .contSig(LogicContSig), .Rd(logic_unit_1_rd));
  Adder #(.width(32)) adder_1 (.a(xor_1_out), .b(Rt), .out(adder_1_out), .cin(decoder_1_out0));  // open: cout
  Comparator #(.width(32)) comparator_1 (
    .a(Rs), .b(multiplexer_1_out), .gt(comparator_1_gt), .eq(comparator_1_eq));  // open: lt
  Comparator #(.width(32), .mode("unsigned")) comparator_2 (
    .a(Rs), .b(multiplexer_1_out), .gt(comparator_2_gt), .eq(comparator_2_eq));  // open: lt
  Multiplexer #(.enable("false")) multiplexer_2 (
    .in0(comparator_1_gt), .in1(comparator_2_gt), .out(flags[0]), .sel(decoder_1_out0));
  Multiplexer #(.enable("false")) multiplexer_3 (
    .in0(comparator_1_eq), .in1(comparator_2_eq), .out(flags[1]), .sel(decoder_1_out1));
  Multiplexer #(.select(2), .width(32), .enable("false")) multiplexer_4 (
    .in0(logic_unit_1_rd), .in1(adder_1_out), .in3(shifter_1_rt), .out(Rd), .sel(ALUContSig));  // open: in2
endmodule
