// Logisim project ALU.circ as structural Verilog: 1 circuit, main circuit ALU
module ALU (
  input  [31:0] BusB,
  input  [31:0] BusA,
  input  [1:0] LogicOp,
  input  [1:0] ShitfOp,
  input  Sub,
  input  Branch,
  input  Unsigned,
  input  [1:0] ALUOp,
  output out_9,
  output out_10,
  output out_11,
  output [31:0] BusD
);

  wire [31:0] arithmeticunit_1_rd, logicunit_1_rd, shifter_1_rt;
  wire [31:1] undriven;

  LogicUnit logicunit_1 (.Rs(BusA), .Rt(BusB), .LogicOp(LogicOp), .Rd(logicunit_1_rd));
  ArithmeticUnit arithmeticunit_1 (.Rs(BusA), .Rs_2(BusB), .Sub(Sub), .Rd(arithmeticunit_1_rd));
  Multiplexer #(.select(2), .width(32), .enable("false")) multiplexer_1 (
    .in0(logicunit_1_rd), .in1(arithmeticunit_1_rd), .in2({undriven, out_11}), .in3(shifter_1_rt),
    .out(BusD), .sel(ALUOp));
  CompareUnit compareunit_1 (
    .Rs(BusA), .Rt(BusB), .Branch(Branch), .Unsigned(Unsigned), .out_5(out_11), .out_6(out_10), .out_7(out_9));
  Shifter shifter_1 (.Rs(BusA), .Imm(BusB[4:0]), .ShiftOp(ShitfOp), .Rt(shifter_1_rt));
endmodule
