// Logisim project ALUControlUnit.circ as structural Verilog: 3 circuits, main circuit ALUControlUnit
module ALUControlUnit (
  input  [1:0] \function ,
  input  [4:0] OPcode,
  output [1:0] ALUOp,
  output [1:0] LogicOp,
  output Sub,
  output [1:0] ShiftOp,
  output Branch,
  output Unsigned
);

  RAM #(.addrWidth(7), .dataWidth(9)) ram_1 (
    .addr({OPcode, \function }), .data({Unsigned, Branch, ShiftOp, Sub, LogicOp, ALUOp}));  // open: sel, clk, ld, clr
endmodule

module ALUControlUnitDecoder (
  input  [4:0] OPcode,
  input  [1:0] \function ,
  output Unsigned,
  output Sub,
  output [1:0] LogicOp,
  output [1:0] ALUOp,
  output [1:0] ShiftOp,
  output Branch
);

  wire and_1_out, and_2_out, and_3_out, and_4_out, decoder_1_out1, decoder_1_out2, decoder_1_out3,
       decoder_1_out4, decoder_1_out5, decoder_1_out6, decoder_1_out7, decoder_1_out20, decoder_1_out24,
       decoder_1_out28, decoder_2_out0, decoder_2_out4, decoder_2_out8, decoder_2_out12, decoder_2_out16,
       decoder_2_out20, decoder_2_out24, decoder_2_out28, decoder_3_out0, decoder_3_out4, decoder_3_out16,
       decoder_3_out17, decoder_3_out18, decoder_3_out19, decoder_3_out20, decoder_3_out21, decoder_3_out24,
       decoder_3_out28, decoder_4_out0, decoder_4_out4;

  and and_1 (and_1_out, ~\function [0], ~\function [1]);  // AND_Gate
  and and_2 (and_2_out, \function [0], ~\function [1]);  // AND_Gate
  and and_3 (and_3_out, ~\function [0], \function [1]);  // AND_Gate
  and and_4 (and_4_out, \function [0], \function [1]);
  Decoder #(.select(5)) decoder_1 (
    .out1(decoder_1_out1), .out2(decoder_1_out2), .out3(decoder_1_out3), .out4(decoder_1_out4),
    .out5(decoder_1_out5), .out6(decoder_1_out6), .out7(decoder_1_out7), .out20(decoder_1_out20),
    .out24(decoder_1_out24), .out28(decoder_1_out28), .sel(OPcode), .en(and_1_out));  // open: out0, out8, out9, out10, out11, out12, out13, out14, out15, out16, out17, out18, out19, out21, out22, out23, out25, out26, out27, out29, out30, out31
  Decoder #(.select(5)) decoder_2 (
    .out0(decoder_2_out0), .out4(decoder_2_out4), .out8(decoder_2_out8), .out12(decoder_2_out12),
    .out16(decoder_2_out16), .out20(decoder_2_out20), .out24(decoder_2_out24), .out28(decoder_2_out28),
    .sel(OPcode), .en(and_2_out));  // open: out1, out2, out3, out5, out6, out7, out9, out10, out11, out13, out14, out15, out17, out18, out19, out21, out22, out23, out25, out26, out27, out29, out30, out31
  Decoder #(.select(5)) decoder_3 (
    .out0(decoder_3_out0), .out4(decoder_3_out4), .out16(decoder_3_out16), .out17(decoder_3_out17),
    .out18(decoder_3_out18), .out19(decoder_3_out19), .out20(decoder_3_out20), .out21(decoder_3_out21),
    .out24(decoder_3_out24), .out28(decoder_3_out28), .sel(OPcode), .en(and_3_out));  // open: out1, out2, out3, out5, out6, out7, out8, out9, out10, out11, out12, out13, out14, out15, out22, out23, out25, out26, out27, out29, out30, out31
  Decoder #(.select(5)) decoder_4 (
    .out0(decoder_4_out0), .out4(decoder_4_out4), .sel(OPcode), .en(and_4_out));  // open: out1, out2, out3, out5, out6, out7, out8, out9, out10, out11, out12, out13, out14, out15, out16, out17, out18, out19, out20, out21, out22, out23, out24, out25, out26, out27, out28, out29, out30, out31
  or or_1 (Unsigned, decoder_1_out7, decoder_2_out12);
  or or_2 (Sub, decoder_1_out5, decoder_2_out4);
  or or_3 (Branch, decoder_3_out16, decoder_3_out17, decoder_3_out18, decoder_3_out19, decoder_3_out20, decoder_3_out21);
  or or_4 (LogicOp[1], decoder_1_out2, decoder_1_out3, decoder_1_out24, decoder_1_out28);
  or or_5 (LogicOp[0], decoder_1_out1, decoder_1_out3, decoder_1_out20, decoder_1_out28);
  or or_6 (ShiftOp[1], decoder_2_out24, decoder_2_out28);
  or or_7 (ShiftOp[0], decoder_2_out20, decoder_2_out28);
  or or_8 (ALUOp[1], decoder_1_out4, decoder_1_out5, decoder_2_out0, decoder_2_out4, decoder_2_out16, decoder_2_out20, decoder_2_out24, decoder_2_out28, decoder_3_out0, decoder_3_out4);
  or or_9 (ALUOp[0], decoder_1_out6, decoder_1_out7, decoder_2_out8, decoder_2_out12, decoder_2_out16, decoder_2_out20, decoder_2_out24, decoder_3_out4, decoder_3_out16, decoder_3_out20, decoder_3_out24, decoder_3_out28, decoder_4_out0, decoder_4_out4);
endmodule

module ALUControlUnitDecoder2 (
  input  [4:0] OPcode,
  input  [1:0] \function ,
  output [1:0] LogicOp,
  output Unsigned,
  output Sub,
  output [1:0] ShiftOp,
  output [1:0] ALUOp,
  output Branch
);

  wire and_1_out, and_2_out, and_3_out, and_4_out, decoder_1_out1, decoder_1_out2, decoder_1_out3,
       decoder_1_out4, decoder_1_out5, decoder_1_out6, decoder_1_out7, decoder_1_out20, decoder_1_out21,
       decoder_1_out22, decoder_1_out23, decoder_1_out24, decoder_1_out25, decoder_1_out26, decoder_1_out27,
       decoder_1_out28, decoder_1_out29, decoder_1_out30, decoder_1_out31, decoder_2_out0, decoder_2_out1,
       decoder_2_out2, decoder_2_out3, decoder_2_out4, decoder_2_out5, decoder_2_out6, decoder_2_out7,
       decoder_2_out8, decoder_2_out9, decoder_2_out10, decoder_2_out11, decoder_2_out12, decoder_2_out13,
       decoder_2_out14, decoder_2_out15, decoder_2_out16, decoder_2_out17, decoder_2_out18, decoder_2_out19,
       decoder_2_out20, decoder_2_out21, decoder_2_out22, decoder_2_out23, decoder_2_out24, decoder_2_out25,
       decoder_2_out26, decoder_2_out27, decoder_2_out28, decoder_2_out29, decoder_2_out30, decoder_2_out31,
       decoder_3_out0, decoder_3_out1, decoder_3_out2, decoder_3_out3, decoder_3_out4, decoder_3_out5,
       decoder_3_out6, decoder_3_out7, decoder_3_out16, decoder_3_out17, decoder_3_out18, decoder_3_out19,
       decoder_3_out20, decoder_3_out21, decoder_3_out22, decoder_3_out23, decoder_3_out24, decoder_3_out25,
       decoder_3_out26, decoder_3_out27, decoder_3_out28, decoder_3_out29, decoder_3_out30, decoder_3_out31,
       decoder_4_out0, decoder_4_out1, decoder_4_out2, decoder_4_out3, decoder_4_out4, decoder_4_out5,
       decoder_4_out6, decoder_4_out7, m1_1, m1_2, m1_3, m1_m2, m2_1, m2_2, or_9_out, or_10_out;

  and and_1 (and_1_out, ~OPcode[4], ~OPcode[3]);  // AND_Gate
  and and_2 (and_2_out, ~OPcode[4], OPcode[3]);  // AND_Gate
  and and_3 (and_3_out, OPcode[4], ~OPcode[3]);  // AND_Gate
  and and_4 (and_4_out, OPcode[4], OPcode[3]);
  Decoder #(.select(5), .disabled(0)) decoder_1 (
    .out1(decoder_1_out1), .out2(decoder_1_out2), .out3(decoder_1_out3), .out4(decoder_1_out4),
    .out5(decoder_1_out5), .out6(decoder_1_out6), .out7(decoder_1_out7), .out20(decoder_1_out20),
    .out21(decoder_1_out21), .out22(decoder_1_out22), .out23(decoder_1_out23), .out24(decoder_1_out24),
    .out25(decoder_1_out25), .out26(decoder_1_out26), .out27(decoder_1_out27), .out28(decoder_1_out28),
    .out29(decoder_1_out29), .out30(decoder_1_out30), .out31(decoder_1_out31),
    .sel({OPcode[2:0], \function }), .en(and_1_out));  // open: out0, out8, out9, out10, out11, out12, out13, out14, out15, out16, out17, out18, out19
  Decoder #(.select(5), .disabled(0)) decoder_2 (
    .out0(decoder_2_out0), .out1(decoder_2_out1), .out2(decoder_2_out2), .out3(decoder_2_out3),
    .out4(decoder_2_out4), .out5(decoder_2_out5), .out6(decoder_2_out6), .out7(decoder_2_out7),
    .out8(decoder_2_out8), .out9(decoder_2_out9), .out10(decoder_2_out10), .out11(decoder_2_out11),
    .out12(decoder_2_out12), .out13(decoder_2_out13), .out14(decoder_2_out14), .out15(decoder_2_out15),
    .out16(decoder_2_out16), .out17(decoder_2_out17), .out18(decoder_2_out18), .out19(decoder_2_out19),
    .out20(decoder_2_out20), .out21(decoder_2_out21), .out22(decoder_2_out22), .out23(decoder_2_out23),
    .out24(decoder_2_out24), .out25(decoder_2_out25), .out26(decoder_2_out26), .out27(decoder_2_out27),
    .out28(decoder_2_out28), .out29(decoder_2_out29), .out30(decoder_2_out30), .out31(decoder_2_out31),
    .sel({OPcode[2:0], \function }), .en(and_2_out));
  Decoder #(.select(5), .disabled(0)) decoder_3 (
    .out0(decoder_3_out0), .out1(decoder_3_out1), .out2(decoder_3_out2), .out3(decoder_3_out3),
    .out4(decoder_3_out4), .out5(decoder_3_out5), .out6(decoder_3_out6), .out7(decoder_3_out7),
    .out16(decoder_3_out16), .out17(decoder_3_out17), .out18(decoder_3_out18), .out19(decoder_3_out19),
    .out20(decoder_3_out20), .out21(decoder_3_out21), .out22(decoder_3_out22), .out23(decoder_3_out23),
    .out24(decoder_3_out24), .out25(decoder_3_out25), .out26(decoder_3_out26), .out27(decoder_3_out27),
    .out28(decoder_3_out28), .out29(decoder_3_out29), .out30(decoder_3_out30), .out31(decoder_3_out31),
    .sel({OPcode[2:0], \function }), .en(and_3_out));  // open: out8, out9, out10, out11, out12, out13, out14, out15
  Decoder #(.select(5), .disabled(0)) decoder_4 (
    .out0(decoder_4_out0), .out1(decoder_4_out1), .out2(decoder_4_out2), .out3(decoder_4_out3),
    .out4(decoder_4_out4), .out5(decoder_4_out5), .out6(decoder_4_out6), .out7(decoder_4_out7),
    .sel({OPcode[2:0], \function }), .en(and_4_out));  // open: out8, out9, out10, out11, out12, out13, out14, out15, out16, out17, out18, out19, out20, out21, out22, out23, out24, out25, out26, out27, out28, out29, out30, out31
  or or_1 (m2_1, decoder_1_out7, decoder_1_out6);
  or or_2 (m1_2, decoder_2_out0, decoder_2_out1, decoder_2_out2, decoder_2_out3, decoder_2_out4, decoder_2_out6, decoder_2_out6, decoder_2_out7);
  or or_3 (m1_3, decoder_3_out0, decoder_3_out1, decoder_3_out2, decoder_3_out3, decoder_3_out4, decoder_3_out5, decoder_3_out6, decoder_3_out7);
  or or_4 (Branch, decoder_3_out16, decoder_3_out17, decoder_3_out18, decoder_3_out19, decoder_3_out20, decoder_3_out21, decoder_3_out22, decoder_3_out23, decoder_3_out24, decoder_3_out25, decoder_3_out26, decoder_3_out27, decoder_3_out28, decoder_3_out29, decoder_3_out30, decoder_3_out31, decoder_4_out0, decoder_4_out1, decoder_4_out2, decoder_4_out3, decoder_4_out4, decoder_4_out5, decoder_4_out6, decoder_4_out7);
  or or_5 (LogicOp[1], or_9_out, decoder_1_out2, decoder_1_out24, decoder_1_out25, decoder_1_out26, decoder_1_out27);
  or or_6 (m1_m2, decoder_2_out16, decoder_2_out17, decoder_2_out18, decoder_2_out19, decoder_2_out20, decoder_2_out21, decoder_2_out22, decoder_2_out23, decoder_2_out24, decoder_2_out25, decoder_2_out26, decoder_2_out27, decoder_2_out28, decoder_2_out29, decoder_2_out30, decoder_2_out31);
  or or_7 (Sub, decoder_1_out5, decoder_2_out4, decoder_2_out5, decoder_2_out6, decoder_2_out7);
  or or_8 (m1_1, decoder_1_out4, decoder_1_out5);
  or or_9 (or_9_out, decoder_1_out3, decoder_1_out28, decoder_1_out29, decoder_1_out30, decoder_1_out31);
  or or_10 (or_10_out, decoder_2_out28, decoder_2_out29, decoder_2_out30, decoder_2_out31);
  or or_11 (LogicOp[0], decoder_1_out1, decoder_1_out20, decoder_1_out21, decoder_1_out22, decoder_1_out23, or_9_out);
  or or_12 (Unsigned, decoder_1_out7, decoder_2_out12, decoder_2_out13, decoder_2_out14, decoder_2_out15);
  or or_13 (ShiftOp[0], decoder_2_out20, decoder_2_out21, decoder_2_out22, decoder_2_out23, or_10_out);
  or or_14 (ShiftOp[1], decoder_2_out24, decoder_2_out25, decoder_2_out26, decoder_2_out27, or_10_out);
  or or_15 (ALUOp[0], m1_1, m1_2, m1_3, m1_m2);
  or or_16 (m2_2, decoder_2_out8, decoder_2_out9, decoder_2_out10, decoder_2_out11, decoder_2_out12, decoder_2_out13, decoder_2_out14, decoder_2_out15);
  or or_17 (ALUOp[1], m2_1, Branch, m2_2, m1_m2);
endmodule
