// Logisim project ArithmeticUnit.circ as structural Verilog: 1 circuit, main circuit ArithmeticUnit
module ArithmeticUnit (
  input  [31:0] Rs,
  input  [31:0] Rs_2,
  input  Sub,
  output [31:0] Rd
);

  wire [31:0] adder_1_out, subtractor_1_out;

  Adder #(.width(32)) adder_1 (.a(Rs), .b(Rs_2), .out(adder_1_out));  // open: cin, cout
  Subtractor #(.width(32)) subtractor_1 (.a(Rs_2), .b(Rs), .out(subtractor_1_out));  // open: bin, bout
  Multiplexer #(.width(32), .enable("false")) multiplexer_1 (
    .in0(adder_1_out), .in1(subtractor_1_out), .out(Rd), .sel(Sub));
endmodule
