// Logisim project BranchJumpSig.circ as structural Verilog: 2 circuits, main circuit BranchJumpSig
module BranchJumpSig (
  input  [4:0] OPcode,
  output BEQZ,
  output BNEZ,
  output BLTZ,
  output BGEZ,
  output BGTZ,
  output BLEZ,
  output JumpR,
  output Jump
);

  wire decoder_1_out26, decoder_1_out27, decoder_1_out30, decoder_1_out31;

  Decoder #(.select(5), .enable("false")) decoder_1 (
    .out20(BEQZ), .out21(BNEZ), .out22(BLTZ), .out23(BGEZ), .out24(BGTZ), .out25(BLEZ),
    .out26(decoder_1_out26), .out27(decoder_1_out27), .out30(decoder_1_out30), .out31(decoder_1_out31),
    .sel(OPcode));  // open: out0, out1, out2, out3, out4, out5, out6, out7, out8, out9, out10, out11, out12, out13, out14, out15, out16, out17, out18, out19, out28, out29
  or or_1 (Jump, decoder_1_out31, decoder_1_out30);
  or or_2 (JumpR, decoder_1_out27, decoder_1_out26);
endmodule

module BranchJumpSig2 (
  input  [4:0] OPcode,
  output killB,
  output BEQZ,
  output BNEZ,
  output BLTZ,
  output BGEZ,
  output BGTZ,
  output BLEZ,
  output JumpR,
  output killJ,
  output Jump
);

  wire decoder_1_out26, decoder_1_out27, decoder_1_out30, decoder_1_out31;

  Decoder #(.select(5), .enable("false")) decoder_1 (
    .out20(BEQZ), .out21(BNEZ), .out22(BLTZ), .out23(BGEZ), .out24(BGTZ), .out25(BLEZ),
    .out26(decoder_1_out26), .out27(decoder_1_out27), .out30(decoder_1_out30), .out31(decoder_1_out31),
    .sel(OPcode));  // open: out0, out1, out2, out3, out4, out5, out6, out7, out8, out9, out10, out11, out12, out13, out14, out15, out16, out17, out18, out19, out28, out29
  or or_1 (killB, BEQZ, BNEZ, BLTZ, BGEZ, BGTZ, BLEZ);
  or or_2 (Jump, decoder_1_out31, decoder_1_out30);
  or or_3 (JumpR, decoder_1_out27, decoder_1_out26);
  or or_4 (killJ, JumpR, Jump);
endmodule
