// Logisim project CompareUnit.circ as structural Verilog: 1 circuit, main circuit CompareUnit
module CompareUnit (
  input  [31:0] Rs,
  input  [31:0] Rt,
  input  Branch,
  input  Unsigned,
  output out_5,
  output out_6,
  output out_7
);

  wire comparator_1_eq, comparator_1_gt, comparator_1_lt, comparator_2_eq, comparator_2_gt, comparator_2_lt;
  wire [31:0] multiplexer_1_out;

  Multiplexer #(.width(32), .enable("false")) multiplexer_1 (
    .in0(Rt), .in1({32{1'b0}}), .out(multiplexer_1_out), .sel(Branch));
  Comparator #(.width(32)) comparator_1 (
    .a(Rs), .b(multiplexer_1_out), .gt(comparator_1_gt), .eq(comparator_1_eq), .lt(comparator_1_lt));
  Comparator #(.width(32), .mode("unsigned")) comparator_2 (
    .a(Rs), .b(multiplexer_1_out), .gt(comparator_2_gt), .eq(comparator_2_eq), .lt(comparator_2_lt));
  Multiplexer #(.enable("false")) multiplexer_2 (
    .in0(comparator_1_lt), .in1(comparator_2_lt), .out(out_5), .sel(Unsigned));
  Multiplexer #(.enable("false")) multiplexer_3 (
    .in0(comparator_1_eq), .in1(comparator_2_eq), .out(out_6), .sel(Unsigned));
  Multiplexer #(.enable("false")) multiplexer_4 (
    .in0(comparator_1_gt), .in1(comparator_2_gt), .out(out_7), .sel(Unsigned));
endmodule
