// Logisim project ForewardUnit.circ as structural Verilog: 5 circuits, main circuit ForewardUnit
module ForewardUnit (
  input  [2:0] Rs,
  input  [2:0] Rt,
  input  [2:0] Rd1,
  input  [2:0] Rd2,
  input  [2:0] Rd3,
  input  rf1,
  input  rf2,
  input  rf3,
  output [1:0] FA,
  output [1:0] FB
);

  wire and_1_out, and_2_out, and_3_out, and_4_out, and_5_out, and_6_out, and_7_out, and_8_out, and_9_out,
       and_10_out, and_11_out, and_12_out;
  wire [2:0] xnor_1_out, xnor_2_out, xnor_3_out, xnor_4_out, xnor_5_out, xnor_6_out;

  assign xnor_1_out = ~(Rs ^ Rd1);  // XNOR_Gate xnor_1, 3 bits wide
  assign xnor_2_out = ~(Rs ^ Rd2);  // XNOR_Gate xnor_2, 3 bits wide
  assign xnor_3_out = ~(Rs ^ Rd3);  // XNOR_Gate xnor_3, 3 bits wide
  and and_1 (and_1_out, xnor_2_out[2], xnor_2_out[1], xnor_2_out[0]);
  and and_2 (and_2_out, xnor_1_out[2], xnor_1_out[1], xnor_1_out[0]);
  and and_3 (and_3_out, and_2_out, rf1);
  and and_4 (and_4_out, and_1_out, rf2);
  and and_5 (and_5_out, xnor_3_out[2], xnor_3_out[1], xnor_3_out[0]);
  and and_6 (and_6_out, and_5_out, rf3);
  assign xnor_4_out = ~(Rt ^ Rd1);  // XNOR_Gate xnor_4, 3 bits wide
  assign xnor_5_out = ~(Rt ^ Rd2);  // XNOR_Gate xnor_5, 3 bits wide
  assign xnor_6_out = ~(Rt ^ Rd3);  // XNOR_Gate xnor_6, 3 bits wide
  and and_7 (and_7_out, xnor_4_out[2], xnor_4_out[1], xnor_4_out[0]);
  and and_8 (and_8_out, xnor_5_out[2], xnor_5_out[1], xnor_5_out[0]);
  and and_9 (and_9_out, xnor_6_out[2], xnor_6_out[1], xnor_6_out[0]);
  and and_10 (and_10_out, and_8_out, rf2);
  and and_11 (and_11_out, and_7_out, rf1);
  and and_12 (and_12_out, and_9_out, rf3);
  or or_1 (FA[0], and_3_out, and_6_out);
  or or_2 (FA[1], and_4_out, and_6_out);
  or or_3 (FB[0], and_11_out, and_12_out);
  or or_4 (FB[1], and_10_out, and_12_out);
endmodule

module ForwardUnit2 (
  input  [2:0] Rt,
  input  [2:0] Rs,
  input  [2:0] Rd1,
  input  [2:0] Rd2,
  input  [2:0] Rd3,
  input  rf1,
  input  rf2,
  input  rf3,
  output [1:0] FA,
  output [1:0] FB
);

  wire and_1_out, and_2_out, and_3_out, and_4_out, and_5_out, and_6_out, comparator_1_eq, comparator_2_eq,
       comparator_3_eq, comparator_4_eq, comparator_5_eq, comparator_6_eq;

  Comparator #(.width(3)) comparator_1 (.a(Rd1), .b(Rt), .eq(comparator_1_eq));  // open: gt, lt
  Comparator #(.width(3)) comparator_2 (.a(Rd2), .b(Rt), .eq(comparator_2_eq));  // open: gt, lt
  Comparator #(.width(3)) comparator_3 (.a(Rd3), .b(Rt), .eq(comparator_3_eq));  // open: gt, lt
  and and_1 (and_1_out, comparator_1_eq, rf1);
  and and_2 (and_2_out, comparator_2_eq, rf2);
  and and_3 (and_3_out, comparator_3_eq, rf3);
  or or_1 (FB[0], and_1_out, and_3_out);
  or or_2 (FB[1], and_2_out, and_3_out);
  Comparator #(.width(3)) comparator_4 (.a(Rd1), .b(Rs), .eq(comparator_4_eq));  // open: gt, lt
  Comparator #(.width(3)) comparator_5 (.a(Rd2), .b(Rs), .eq(comparator_5_eq));  // open: gt, lt
  Comparator #(.width(3)) comparator_6 (.a(Rd3), .b(Rs), .eq(comparator_6_eq));  // open: gt, lt
  and and_4 (and_4_out, comparator_4_eq, rf1);
  and and_5 (and_5_out, comparator_5_eq, rf2);
  and and_6 (and_6_out, comparator_6_eq, rf3);
  or or_3 (FA[0], and_4_out, and_6_out);
  or or_4 (FA[1], and_5_out, and_6_out);
endmodule

module ForwardStall (
  input  [2:0] Rt,
  input  [2:0] Rs,
  input  [2:0] Rd1,
  input  [2:0] Rd2,
  input  [2:0] Rd3,
  input  rf1,
  input  rf2,
  input  rf3,
  input  ld,
  output [1:0] FA,
  output stall,
  output [1:0] FB
);

  wire and_1_out, and_2_out, and_3_out, and_4_out, and_5_out, and_6_out, comparator_1_eq, comparator_2_eq,
       comparator_3_eq, comparator_4_eq, comparator_5_eq, comparator_6_eq, or_5_out;

  Comparator #(.width(3)) comparator_1 (.a(Rd1), .b(Rt), .eq(comparator_1_eq));  // open: gt, lt
  Comparator #(.width(3)) comparator_2 (.a(Rd2), .b(Rt), .eq(comparator_2_eq));  // open: gt, lt
  Comparator #(.width(3)) comparator_3 (.a(Rd3), .b(Rt), .eq(comparator_3_eq));  // open: gt, lt
  and and_1 (and_1_out, comparator_1_eq, rf1);
  and and_2 (and_2_out, comparator_2_eq, rf2);
  and and_3 (and_3_out, comparator_3_eq, rf3);
  or or_1 (FB[0], and_1_out, and_3_out);
  or or_2 (FB[1], and_2_out, and_3_out);
  Comparator #(.width(3)) comparator_4 (.a(Rd1), .b(Rs), .eq(comparator_4_eq));  // open: gt, lt
  Comparator #(.width(3)) comparator_5 (.a(Rd2), .b(Rs), .eq(comparator_5_eq));  // open: gt, lt
  Comparator #(.width(3)) comparator_6 (.a(Rd3), .b(Rs), .eq(comparator_6_eq));  // open: gt, lt
  and and_4 (and_4_out, comparator_4_eq, rf1);
  and and_5 (and_5_out, comparator_5_eq, rf2);
  and and_6 (and_6_out, comparator_6_eq, rf3);
  or or_3 (FA[0], and_4_out, and_6_out);
  or or_4 (FA[1], and_5_out, and_6_out);
  or or_5 (or_5_out, and_4_out, and_1_out);
  and and_7 (stall, or_5_out, ld);
endmodule

module ForwardUnit3 (
  input  [2:0] Rt,
  input  [2:0] Rs,
  input  [2:0] Rd1,
  input  [2:0] Rd2,
  input  [2:0] Rd3,
  input  rf1,
  input  rf2,
  input  rf3,
  output [1:0] FA,
  output [1:0] FB
);

  wire and_1_out, and_2_out, and_3_out, and_4_out, and_5_out, and_6_out, and_7_out, and_8_out, and_9_out,
       and_10_out, comparator_1_eq, comparator_2_eq, comparator_3_eq, comparator_4_eq, comparator_5_eq,
       comparator_6_eq;

  Comparator #(.width(3)) comparator_1 (.a(Rd1), .b(Rt), .eq(comparator_1_eq));  // open: gt, lt
  Comparator #(.width(3)) comparator_2 (.a(Rd2), .b(Rt), .eq(comparator_2_eq));  // open: gt, lt
  Comparator #(.width(3)) comparator_3 (.a(Rd3), .b(Rt), .eq(comparator_3_eq));  // open: gt, lt
  and and_1 (and_1_out, comparator_1_eq, rf1);
  and and_2 (and_2_out, comparator_2_eq, rf2);
  and and_3 (and_3_out, comparator_3_eq, rf3);
  Comparator #(.width(3)) comparator_4 (.a(Rd1), .b(Rs), .eq(comparator_4_eq));  // open: gt, lt
  Comparator #(.width(3)) comparator_5 (.a(Rd2), .b(Rs), .eq(comparator_5_eq));  // open: gt, lt
  Comparator #(.width(3)) comparator_6 (.a(Rd3), .b(Rs), .eq(comparator_6_eq));  // open: gt, lt
  and and_4 (and_4_out, ~and_1_out, and_2_out);  // AND_Gate
  and and_5 (and_5_out, ~and_4_out, and_3_out);  // AND_Gate
  and and_6 (and_6_out, comparator_4_eq, rf1);
  and and_7 (and_7_out, comparator_5_eq, rf2);
  and and_8 (and_8_out, comparator_6_eq, rf3);
  or or_1 (FB[0], and_1_out, and_5_out);
  or or_2 (FB[1], and_4_out, and_5_out);
  and and_9 (and_9_out, ~and_6_out, and_7_out);  // AND_Gate
  and and_10 (and_10_out, ~and_9_out, and_8_out);  // AND_Gate
  or or_3 (FA[0], and_6_out, and_10_out);
  or or_4 (FA[1], and_9_out, and_10_out);
endmodule

module ForwardStall2 (
  input  [2:0] Rt,
  input  [2:0] Rs,
  input  [2:0] Rd1,
  input  [2:0] Rd2,
  input  [2:0] Rd3,
  input  rf1,
  input  rf2,
  input  rf3,
  input  ld,
  output [1:0] FA,
  output stall,
  output [1:0] FB
);

  wire and_1_out, and_2_out, and_3_out, and_4_out, and_5_out, and_6_out, and_7_out, and_8_out, and_9_out,
       and_10_out, comparator_1_eq, comparator_2_eq, comparator_3_eq, comparator_4_eq, comparator_5_eq,
       comparator_6_eq, or_5_out;

  Comparator #(.width(3)) comparator_1 (.a(Rd1), .b(Rt), .eq(comparator_1_eq));  // open: gt, lt
  Comparator #(.width(3)) comparator_2 (.a(Rd2), .b(Rt), .eq(comparator_2_eq));  // open: gt, lt
  Comparator #(.width(3)) comparator_3 (.a(Rd3), .b(Rt), .eq(comparator_3_eq));  // open: gt, lt
  and and_1 (and_1_out, comparator_1_eq, rf1);
  and and_2 (and_2_out, comparator_2_eq, rf2);
  and and_3 (and_3_out, comparator_3_eq, rf3);
  Comparator #(.width(3)) comparator_4 (.a(Rd1), .b(Rs), .eq(comparator_4_eq));  // open: gt, lt
  Comparator #(.width(3)) comparator_5 (.a(Rd2), .b(Rs), .eq(comparator_5_eq));  // open: gt, lt
  Comparator #(.width(3)) comparator_6 (.a(Rd3), .b(Rs), .eq(comparator_6_eq));  // open: gt, lt
  and and_4 (and_4_out, ~and_1_out, and_2_out);  // AND_Gate
  and and_5 (and_5_out, ~and_4_out, and_3_out);  // AND_Gate
  and and_6 (and_6_out, comparator_4_eq, rf1);
  and and_7 (and_7_out, comparator_5_eq, rf2);
  and and_8 (and_8_out, comparator_6_eq, rf3);
  or or_1 (FB[0], and_1_out, and_5_out);
  or or_2 (FB[1], and_4_out, and_5_out);
  and and_9 (and_9_out, ~and_6_out, and_7_out);  // AND_Gate
  and and_10 (and_10_out, ~and_9_out, and_8_out);  // AND_Gate
  or or_3 (FA[0], and_6_out, and_10_out);
  or or_4 (FA[1], and_9_out, and_10_out);
  or or_5 (or_5_out, and_6_out, and_1_out);
  and and_11 (stall, or_5_out, ld);
endmodule
