// Logisim project LogicUnit.circ as structural Verilog: 1 circuit, main circuit LogicUnit
module LogicUnit (
  input  [31:0] Rs,
  input  [31:0] Rt,
  input  [1:0] LogicOp,
  output [31:0] Rd
);

  wire [31:0] and_1_out, and_2_out, or_1_out, xor_1_out;

  assign and_1_out = Rs & Rt;  // AND_Gate and_1, 32 bits wide
  assign and_2_out = ~Rs & Rt;  // AND_Gate and_2, 32 bits wide
  assign or_1_out = Rs | Rt;  // OR_Gate or_1, 32 bits wide
  assign xor_1_out = Rs ^ Rt;  // XOR_Gate xor_1, 32 bits wide
  Multiplexer #(.select(2), .width(32), .enable("false")) multiplexer_1 (
    .in0(and_1_out), .in1(and_2_out), .in2(or_1_out), .in3(xor_1_out), .out(Rd), .sel(LogicOp));
endmodule
