// Logisim project RegisterFile.circ as structural Verilog: 1 circuit, main circuit 8-32-bit RegisterFile
module _8_32_bit_RegisterFile (
  input  [2:0] Rd,
  input  writeSig,
  input  [2:0] Rs,
  input  CLK,
  input  [2:0] Rt,
  output [31:0] sBus,
  output [31:0] tBus
);

  wire and_1_out, and_2_out, and_3_out, and_4_out, and_5_out, and_6_out, and_7_out, and_8_out, buf0, buf1,
       buf2, buf3, buf4, buf5, buf6, buf7, buf8, buf9, buf10, buf11, buf12, buf13, buf14, buf15,
       decoder_1_out0, decoder_1_out1, decoder_1_out2, decoder_1_out3, decoder_1_out4, decoder_1_out5,
       decoder_1_out6, decoder_1_out7;
  wire [31:0] r0_q, r1_q, r2_q, r3_q, r4_q, r5_q, r6_q, r7_q, undriven;

  and and_1 (and_1_out, decoder_1_out0, writeSig);
  Decoder #(.select(3), .enable("false")) decoder_1 (
    .out0(decoder_1_out0), .out1(decoder_1_out1), .out2(decoder_1_out2), .out3(decoder_1_out3),
    .out4(decoder_1_out4), .out5(decoder_1_out5), .out6(decoder_1_out6), .out7(decoder_1_out7), .sel(Rd));
  Register #(.width(32)) r0 (.D(undriven), .en(and_1_out), .Q(r0_q), .clk(CLK));  // open: clr
  and and_2 (and_2_out, decoder_1_out1, writeSig);
  Register #(.width(32)) r1 (.D(undriven), .en(and_2_out), .Q(r1_q), .clk(CLK));  // open: clr
  assign sBus = buf0 ? r0_q : 32'bz;  // Controlled_Buffer controlled_buffer_1
  assign tBus = buf8 ? r0_q : 32'bz;  // Controlled_Buffer controlled_buffer_2
  and and_3 (and_3_out, decoder_1_out2, writeSig);
  Register #(.width(32)) r2 (.D(undriven), .en(and_3_out), .Q(r2_q), .clk(CLK));  // open: clr
  assign sBus = buf1 ? r1_q : 32'bz;  // Controlled_Buffer controlled_buffer_3
  assign tBus = buf9 ? r1_q : 32'bz;  // Controlled_Buffer controlled_buffer_4
  and and_4 (and_4_out, decoder_1_out3, writeSig);
  assign tBus = buf10 ? r2_q : 32'bz;  // Controlled_Buffer controlled_buffer_5
  and and_5 (and_5_out, decoder_1_out4, writeSig);
  Register #(.width(32)) r3 (.D(undriven), .en(and_4_out), .Q(r3_q), .clk(CLK));  // open: clr
  assign sBus = buf2 ? r2_q : 32'bz;  // Controlled_Buffer controlled_buffer_6
  and and_6 (and_6_out, decoder_1_out5, writeSig);
  Register #(.width(32)) r4 (.D(undriven), .en(and_5_out), .Q(r4_q), .clk(CLK));  // open: clr
  assign sBus = buf3 ? r3_q : 32'bz;  // Controlled_Buffer controlled_buffer_7
  assign tBus = buf11 ? r3_q : 32'bz;  // Controlled_Buffer controlled_buffer_8
  Register #(.width(32)) r5 (.D(undriven), .en(and_6_out), .Q(r5_q), .clk(CLK));  // open: clr
  assign sBus = buf4 ? r4_q : 32'bz;  // Controlled_Buffer controlled_buffer_9
  assign tBus = buf12 ? r4_q : 32'bz;  // Controlled_Buffer controlled_buffer_10
  and and_7 (and_7_out, decoder_1_out6, writeSig);
  Register #(.width(32)) r6 (.D(undriven), .en(and_7_out), .Q(r6_q), .clk(CLK));  // open: clr
  assign sBus = buf5 ? r5_q : 32'bz;  // Controlled_Buffer controlled_buffer_11
  assign tBus = buf13 ? r5_q : 32'bz;  // Controlled_Buffer controlled_buffer_12
  and and_8 (and_8_out, decoder_1_out7, writeSig);
  assign sBus = buf6 ? r6_q : 32'bz;  // Controlled_Buffer controlled_buffer_13
  assign tBus = buf14 ? r6_q : 32'bz;  // Controlled_Buffer controlled_buffer_14
  Register #(.width(32)) r7 (.D(undriven), .en(and_8_out), .Q(r7_q), .clk(CLK));  // open: clr
  Decoder #(.select(3), .enable("false")) decoder_2 (
    .out0(buf0), .out1(buf1), .out2(buf2), .out3(buf3), .out4(buf4), .out5(buf5), .out6(buf6), .out7(buf7),
    .sel(Rs));
  Decoder #(.select(3), .enable("false")) decoder_3 (
    .out0(buf8), .out1(buf9), .out2(buf10), .out3(buf11), .out4(buf12), .out5(buf13), .out6(buf14),
    .out7(buf15), .sel(Rt));
  assign sBus = buf7 ? r7_q : 32'bz;  // Controlled_Buffer controlled_buffer_15
  assign tBus = buf15 ? r7_q : 32'bz;  // Controlled_Buffer controlled_buffer_16
endmodule
