// Logisim project Shifter.circ as structural Verilog: 1 circuit, main circuit Shifter
module Shifter (
  input  [31:0] Rs,
  input  [4:0] Imm,
  input  [1:0] ShiftOp,
  output [31:0] Rt
);

  wire [31:0] shifter_1_out, shifter_2_out, shifter_3_out, shifter_4_out;

  Shifter_part #(.width(32)) shifter_1 (.in(Rs), .\dist (Imm), .out(shifter_1_out));
  Shifter_part #(.width(32), .shift("lr")) shifter_2 (.in(Rs), .\dist (Imm), .out(shifter_2_out));
  Shifter_part #(.width(32), .shift("ar")) shifter_3 (.in(Rs), .\dist (Imm), .out(shifter_3_out));
  Shifter_part #(.width(32), .shift("rr")) shifter_4 (.in(Rs), .\dist (Imm), .out(shifter_4_out));
  Multiplexer #(.select(2), .width(32), .enable("false")) multiplexer_1 (
    .in0(shifter_1_out), .in1(shifter_2_out), .in2(shifter_3_out), .in3(shifter_4_out), .out(Rt),
    .sel(ShiftOp));
endmodule
