// Logisim project MiainControlUnit.circ as structural Verilog: 1 circuit, main circuit MainControlUnit
module MainControlUnit (
  input  [4:0] OPcode,
  output ALUSrc,
  output [1:0] regDest,
  output ld,
  output str,
  output en,
  output [1:0] extOp,
  output [1:0] wb,
  output rf
);

  wire decoder_1_out2, decoder_1_out3, decoder_1_out4, decoder_1_out5, decoder_1_out6, decoder_1_out7,
       decoder_1_out8, decoder_1_out9, decoder_1_out10, decoder_1_out11, decoder_1_out12, decoder_1_out13,
       decoder_1_out14, decoder_1_out15, decoder_1_out18, decoder_1_out19, decoder_1_out20, decoder_1_out21,
       decoder_1_out22, decoder_1_out23, decoder_1_out24, decoder_1_out25, decoder_1_out26, decoder_1_out27,
       decoder_1_out28, decoder_1_out29, decoder_1_out30, decoder_1_out31;
  wire [1:0] bit_extender_1_out;
  wire [1:1] or_3_out;

  Decoder #(.select(5), .enable("false")) decoder_1 (
    .out2(decoder_1_out2), .out3(decoder_1_out3), .out4(decoder_1_out4), .out5(decoder_1_out5),
    .out6(decoder_1_out6), .out7(decoder_1_out7), .out8(decoder_1_out8), .out9(decoder_1_out9),
    .out10(decoder_1_out10), .out11(decoder_1_out11), .out12(decoder_1_out12), .out13(decoder_1_out13),
    .out14(decoder_1_out14), .out15(decoder_1_out15), .out16(ld), .out17(str), .out18(decoder_1_out18),
    .out19(decoder_1_out19), .out20(decoder_1_out20), .out21(decoder_1_out21), .out22(decoder_1_out22),
    .out23(decoder_1_out23), .out24(decoder_1_out24), .out25(decoder_1_out25), .out26(decoder_1_out26),
    .out27(decoder_1_out27), .out28(decoder_1_out28), .out29(decoder_1_out29), .out30(decoder_1_out30),
    .out31(decoder_1_out31), .sel(OPcode));  // open: out0, out1
  or or_1 (ALUSrc, decoder_1_out4, decoder_1_out5, decoder_1_out6, decoder_1_out7, decoder_1_out8, decoder_1_out9, decoder_1_out10, decoder_1_out11, decoder_1_out12, decoder_1_out13, decoder_1_out14, decoder_1_out15, str, ld, decoder_1_out26, decoder_1_out27, decoder_1_out28, decoder_1_out29, decoder_1_out31);
  or or_2 (extOp[1], decoder_1_out31, decoder_1_out30, decoder_1_out29, decoder_1_out28);
  nor nor_1 (rf, decoder_1_out18, decoder_1_out19, decoder_1_out2, decoder_1_out3, decoder_1_out30, decoder_1_out20, decoder_1_out21, decoder_1_out22, decoder_1_out23, decoder_1_out24, decoder_1_out25, decoder_1_out26, str);
  or or_3 (or_3_out[1], decoder_1_out27, decoder_1_out31);
  assign bit_extender_1_out = {{1{decoder_1_out28}}, decoder_1_out28};  // Bit_Extender bit_extender_1
  assign wb = bit_extender_1_out | {or_3_out[1], ld};  // OR_Gate or_4, 2 bits wide
  or or_5 (extOp[0], decoder_1_out20, decoder_1_out21, decoder_1_out22, decoder_1_out23, decoder_1_out24, decoder_1_out25, decoder_1_out26, decoder_1_out27);
  or or_6 (en, ld, str);
  or or_7 (regDest[0], decoder_1_out4, decoder_1_out5, decoder_1_out6, decoder_1_out7, decoder_1_out8, decoder_1_out9, decoder_1_out10, decoder_1_out11, decoder_1_out12, decoder_1_out13, decoder_1_out14, decoder_1_out15, ld, decoder_1_out28, decoder_1_out29);
  or or_8 (regDest[1], decoder_1_out27, decoder_1_out28, decoder_1_out29, decoder_1_out31);
endmodule
