// Logisim project cpu.circ as structural Verilog
module RegisterFile (
  input  [2:0] in_1,
  input  in_2,
  input  [2:0] in_3,
  input  [31:0] in_4,
  input  [2:0] in_5,
  output [31:0] out_6,
  output [31:0] out_7
);

  wire and_1_out, and_2_out, and_3_out, and_4_out, and_5_out, and_6_out, and_7_out, and_8_out, buf0, buf1,
       buf2, buf3, buf4, buf5, buf6, buf7, buf8, buf9, buf10, buf11, buf12, buf13, buf14, buf15, clock_1_out,
       decoder_1_out0, decoder_1_out1, decoder_1_out2, decoder_1_out3, decoder_1_out4, decoder_1_out5,
       decoder_1_out6, decoder_1_out7;
  wire [31:0] r0_q, r1_q, r2_q, r3_q, r4_q, r5_q, r6_q, r7_q;

  and and_1 (and_1_out, decoder_1_out0, in_2);
  Clock clock_1 (.out(clock_1_out));
  Decoder #(.select(3), .enable("false")) decoder_1 (
    .out0(decoder_1_out0), .out1(decoder_1_out1), .out2(decoder_1_out2), .out3(decoder_1_out3),
    .out4(decoder_1_out4), .out5(decoder_1_out5), .out6(decoder_1_out6), .out7(decoder_1_out7), .sel(in_1));
  Register #(.width(32)) r0 (.D(in_4), .en(and_1_out), .Q(r0_q), .clk(clock_1_out));  // open: clr
  and and_2 (and_2_out, decoder_1_out1, in_2);
  Register #(.width(32)) r1 (.D(in_4), .en(and_2_out), .Q(r1_q), .clk(clock_1_out));  // open: clr
  assign out_6 = buf0 ? r0_q : 32'bz;  // Controlled_Buffer controlled_buffer_1
  assign out_7 = buf8 ? r0_q : 32'bz;  // Controlled_Buffer controlled_buffer_2
  and and_3 (and_3_out, decoder_1_out2, in_2);
  Register #(.width(32)) r2 (.D(in_4), .en(and_3_out), .Q(r2_q), .clk(clock_1_out));  // open: clr
  assign out_6 = buf1 ? r1_q : 32'bz;  // Controlled_Buffer controlled_buffer_3
  assign out_7 = buf9 ? r1_q : 32'bz;  // Controlled_Buffer controlled_buffer_4
  and and_4 (and_4_out, decoder_1_out3, in_2);
  assign out_7 = buf10 ? r2_q : 32'bz;  // Controlled_Buffer controlled_buffer_5
  and and_5 (and_5_out, decoder_1_out4, in_2);
  Register #(.width(32)) r3 (.D(in_4), .en(and_4_out), .Q(r3_q), .clk(clock_1_out));  // open: clr
  assign out_6 = buf2 ? r2_q : 32'bz;  // Controlled_Buffer controlled_buffer_6
  and and_6 (and_6_out, decoder_1_out5, in_2);
  Register #(.width(32)) r4 (.D(in_4), .en(and_5_out), .Q(r4_q), .clk(clock_1_out));  // open: clr
  assign out_6 = buf3 ? r3_q : 32'bz;  // Controlled_Buffer controlled_buffer_7
  assign out_7 = buf11 ? r3_q : 32'bz;  // Controlled_Buffer controlled_buffer_8
  Register #(.width(32)) r5 (.D(in_4), .en(and_6_out), .Q(r5_q), .clk(clock_1_out));  // open: clr
  assign out_6 = buf4 ? r4_q : 32'bz;  // Controlled_Buffer controlled_buffer_9
  assign out_7 = buf12 ? r4_q : 32'bz;  // Controlled_Buffer controlled_buffer_10
  and and_7 (and_7_out, decoder_1_out6, in_2);
  Register #(.width(32)) r6 (.D(in_4), .en(and_7_out), .Q(r6_q), .clk(clock_1_out));  // open: clr
  assign out_6 = buf5 ? r5_q : 32'bz;  // Controlled_Buffer controlled_buffer_11
  assign out_7 = buf13 ? r5_q : 32'bz;  // Controlled_Buffer controlled_buffer_12
  and and_8 (and_8_out, decoder_1_out7, in_2);
  assign out_6 = buf6 ? r6_q : 32'bz;  // Controlled_Buffer controlled_buffer_13
  assign out_7 = buf14 ? r6_q : 32'bz;  // Controlled_Buffer controlled_buffer_14
  Register #(.width(32)) r7 (.D(in_4), .en(and_8_out), .Q(r7_q), .clk(clock_1_out));  // open: clr
  Decoder #(.select(3), .enable("false")) decoder_2 (
    .out0(buf0), .out1(buf1), .out2(buf2), .out3(buf3), .out4(buf4), .out5(buf5), .out6(buf6), .out7(buf7),
    .sel(in_3));
  Decoder #(.select(3), .enable("false")) decoder_3 (
    .out0(buf8), .out1(buf9), .out2(buf10), .out3(buf11), .out4(buf12), .out5(buf13), .out6(buf14),
    .out7(buf15), .sel(in_5));
  assign out_6 = buf7 ? r7_q : 32'bz;  // Controlled_Buffer controlled_buffer_15
  assign out_7 = buf15 ? r7_q : 32'bz;  // Controlled_Buffer controlled_buffer_16
endmodule
